# Fritzing sketch all_with_welder_non_kit (saved by Fritzing 0.9.3b)
breadboards: 1

parts:
  U1 = Arduino Uno (Rev3) - ICSP
  R3 = Resistor [tolerance=±5% resistance=1k package="2010 [SMD]"]
  LED2 = smd LED [color="Yellow (585nm)" package="0805 [SMD]"]
  R4 = Resistor [tolerance=±5% resistance=1k package="2010 [SMD]"]
  LED5 = smd LED [color="Red (633nm)" package="0805 [SMD]"]
  RL1 = PHOTOCELL [package=photocell-kit]
  R1 = Resistor [tolerance=±5% resistance=10k package="2010 [SMD]"]
  Servo1 = Basic Servo
  R6 = Resistor [tolerance=±5% resistance=1k package="2010 [SMD]"]
  R7 = Resistor [tolerance=±5% resistance=1k package="2010 [SMD]"]
  LED7 = smd LED [color="White (6500K)" package="0805 [SMD]"]
  LED4 = smd LED [color="White (6500K)" package="0805 [SMD]"]
  R5 = Resistor [tolerance=±5% resistance=1k package="2010 [SMD]"]
  LED6 = smd LED [color="Blue (430nm)" package="0805 [SMD]"]

nets:
  N1: U1.A0, RL1.P$1, R1.Pin_1
  5V: U1.5V, RL1.P$2, Servo1.vcc
  N2: U1.ICSP_MOSI, U1.D11_PWM/MOSI, LED7.anode
  GND: U1.GND, R3.Pin_0, R4.Pin_0, R1.Pin_0, Servo1.gnd, R6.Pin_0, R7.Pin_0, R5.Pin_0
  N3: U1.D9_PWM, Servo1.pulse
  N4: U1.D3_PWM, LED4.anode
  N5: U1.D4, LED6.anode
  N6: U1.D5_PWM, LED5.anode
  N7: U1.D6_PWM, LED2.anode
  N8: R3.Pin_1, LED5.cathode
  N9: LED2.cathode, R4.Pin_1
  N10: R6.Pin_1, LED4.cathode
  N11: R7.Pin_1, LED7.cathode
  N12: R5.Pin_1, LED6.cathode
