# Fritzing sketch add_two_leds (saved by Fritzing 0.9.10b)
breadboards: 1

parts:
  U1 = Arduino Uno (Rev3) - ICSP
  R3 = Resistor [tolerance=±5% resistance=1k package="2010 [SMD]"]
  LED2 = smd LED [color="Yellow (585nm)" package="0805 [SMD]"]
  R4 = Resistor [tolerance=±5% resistance=1k package="2010 [SMD]"]
  LED5 = smd LED [color="Red (633nm)" package="0805 [SMD]"]

nets:
  N1: U1.GND, R3.Pin_0, R4.Pin_0
  N2: U1.D5_PWM, LED2.anode
  N3: U1.D6_PWM, LED5.anode
  N4: R3.Pin_1, LED2.cathode
  N5: R4.Pin_1, LED5.cathode
