# Fritzing sketch all (saved by Fritzing 0.9.10b)
breadboards: 1

parts:
  U1 = Arduino Uno (Rev3) - ICSP
  R1 = Resistor [tolerance=±5% resistance=10k package="2010 [SMD]"]
  RL1 = PHOTOCELL [package=photocell-kit]
  Servo1 = Basic Servo
  R2 = Resistor [tolerance=±5% resistance=1k package="2010 [SMD]"]
  R3 = Resistor [tolerance=±5% resistance=1k package="2010 [SMD]"]
  LED2 = smd LED [color="Yellow (585nm)" package="0805 [SMD]"]
  R4 = Resistor [tolerance=±5% resistance=1k package="2010 [SMD]"]
  LED4 = smd LED [color="Green (555nm)" package="0805 [SMD]"]
  R5 = Resistor [tolerance=±5% resistance=1k package="2010 [SMD]"]
  LED5 = smd LED [color="Red (633nm)" package="0805 [SMD]"]
  LED6 = smd LED [color="Blue (430nm)" package="0805 [SMD]"]

nets:
  N1: U1.A0, R1.Pin_1, RL1.P$1
  5V: U1.5V, RL1.P$2, Servo1.vcc
  N2: U1.ICSP_MOSI, Servo1.pulse
  GND: U1.GND, R1.Pin_0, Servo1.gnd, R2.Pin_0, R3.Pin_0, R4.Pin_0, R5.Pin_0
  N3: U1.D9_PWM, LED6.anode
  N4: U1.D3_PWM, LED4.anode
  N5: U1.D5_PWM, LED2.anode
  N6: U1.D6_PWM, LED5.anode
  N7: R2.Pin_1, LED4.cathode
  N8: R3.Pin_1, LED2.cathode
  N9: R4.Pin_1, LED5.cathode
  N10: R5.Pin_1, LED6.cathode
