# Fritzing sketch STL_clinic_2022_Beacon (saved by Fritzing 0.9.3b)
breadboards: 1

parts:
  U1 = Arduino Nano (Rev3.0) (ICSP)
  R1 = Resistor [tolerance=±5% resistance=1k package=THT]
  LED1 = smd LED [color="Yellow (585nm)" package="0805 [SMD]"]

nets:
  N1: U1.GND, R1.Pin_0
  N2: U1.A5, LED1.anode
  N3: R1.Pin_1, LED1.cathode
