# Fritzing sketch STL_clinic_2022_All_NoPower_NoBeacon_NoDistance (saved by Fritzing 0.9.3b)
breadboards: 1

parts:
  DFRobot_DFPlayer_Mini1 = DFRobot DFPlayer Mini [part_number=DFR0299]
  U1 = Arduino Nano (Rev3.0) (ICSP)
  SP1 = SPEAKER [package=pcb_mount_speaker]

nets:
  VCC: DFRobot_DFPlayer_Mini1.VCC, U1.5V
  N1: DFRobot_DFPlayer_Mini1.RX, U1.D3
  N2: DFRobot_DFPlayer_Mini1.TX, U1.D2
  N3: DFRobot_DFPlayer_Mini1.SPK_1, SP1.+
  N4: DFRobot_DFPlayer_Mini1.GND-1, DFRobot_DFPlayer_Mini1.GND-2, U1.GND
  N5: DFRobot_DFPlayer_Mini1.SPK_2, SP1.-
