# Fritzing sketch allTogether_oneServo (saved by Fritzing 0.9.3b)
breadboards: 1

parts:
  Uno = Arduino Uno (Rev3) - ICSP
  LED1 = LED - 3mm [color="Green (560nm)" package="3 mm [THT]"]
  R1 = Resistor [tolerance=±5% resistance=1k package=THT]
  LED2 = LED - 3mm [color="Red (633nm)" package="3 mm [THT]"]
  R2 = Resistor [tolerance=±5% resistance=1k package=THT]
  LED3 = LED - 3mm [color="Red (633nm)" package="3 mm [THT]"]
  R3 = Resistor [tolerance=±5% resistance=1k package=THT]
  LED4 = LED - 3mm [color="Red (633nm)" package="3 mm [THT]"]
  R4 = Resistor [tolerance=±5% resistance=1k package=THT]
  S1 = Pushbutton [package="[THT]"]
  R5 = Photocell (LDR) [package=THT]
  R6 = Resistor [tolerance=±5% resistance=10k package=THT]
  JP1 = Header 2 [package=molex-1x2_lock]
  J1 = Basic Servo
  LED5 = LED - 3mm [color="Red (633nm)" package="3 mm [THT]"]
  LED6 = LED - 3mm [color="Red (633nm)" package="3 mm [THT]"]
  LED7 = LED - 3mm [color="Red (633nm)" package="3 mm [THT]"]
  R7 = Resistor [tolerance=±5% resistance=1k package=THT]
  R8 = Resistor [tolerance=±5% resistance=1k package=THT]
  R9 = Resistor [tolerance=±5% resistance=1k package=THT]

nets:
  N1: Uno.A0, R5.pin_0, R6.Pin_0
  GND: Uno.GND, R1.Pin_1, R2.Pin_1, R3.Pin_1, R4.Pin_1, S1.Pin_1, S1.Pin_2, R6.Pin_1, JP1.2, J1.gnd, R7.Pin_1, R8.Pin_1, R9.Pin_1
  N2: Uno.D8, S1.Pin_3, S1.Pin_4
  N3: Uno.D10_PWM/SS, LED4.anode, LED5.anode
  N4: Uno.D11_PWM/MOSI, LED3.anode, LED7.anode
  N5: Uno.D12/MISO, LED2.anode, LED6.anode
  N6: Uno.D13/SCK, LED1.anode
  N7: Uno.D6_PWM, J1.pulse
  N8: Uno.D7, JP1.1
  5V: Uno.5V, R5.pin_1, J1.vcc
  N9: LED1.cathode, R1.Pin_0
  N10: LED2.cathode, R2.Pin_0
  N11: LED3.cathode, R3.Pin_0
  N12: LED4.cathode, R4.Pin_0
  N13: LED5.cathode, R7.Pin_0
  N14: LED6.cathode, R9.Pin_0
  N15: LED7.cathode, R8.Pin_0
