# Fritzing sketch campfire_by_light (saved by Fritzing 0.9.3b)
breadboards: 1

parts:
  U1 = Arduino Uno (Rev3) - ICSP
  R3 = Resistor [tolerance=±5% resistance=1k package="2010 [SMD]"]
  LED2 = smd LED [color="Yellow (585nm)" package="0805 [SMD]"]
  R4 = Resistor [tolerance=±5% resistance=1k package="2010 [SMD]"]
  LED5 = smd LED [color="Red (633nm)" package="0805 [SMD]"]
  RL1 = PHOTOCELL [package=photocell-kit]
  R1 = Resistor [tolerance=±5% resistance=10k package="2010 [SMD]"]

nets:
  N1: U1.A0, RL1.P$2, R1.Pin_1
  N2: U1.GND, R3.Pin_0, R4.Pin_0, R1.Pin_0
  N3: U1.5V, RL1.P$1
  N4: U1.D5_PWM, LED5.anode
  N5: U1.D6_PWM, LED2.anode
  N6: R3.Pin_1, LED5.cathode
  N7: LED2.cathode, R4.Pin_1
