# Fritzing sketch NodeMCU-relay (saved by Fritzing 0.9.10b)

parts:
  U1 = NodeMCU V1.0
  KY-1 = Keyes Relay [package=THT]

nets:
  N1: U1.D4, KY-1.signal
  N2: U1.3V3, KY-1.power
  N3: U1.GND, U1.D5, KY-1.ground

notes:
  https://github.com/mwittig/pimatic-fritzing-sketches
  fritzing drawing credit to the pimatic community:

custom parts:
  NodeMCU V1.0: ESP9266 based NodeMCU
  Keyes Relay: The Keyes 5V relay module is suitable for SCM development, home appliance control. It uses a 5V~12V TIL control signal which can control DC / AC signal.
